# Fritzing sketch EPS_outdoor (saved by Fritzing 1.0.6)
circuit board: 3.7cm x 3.5cm
circuit board: 1.8cm x 3.5cm
breadboards: 3

parts:
  ESP_outdoor = Esp32-c3 super mini
  J1 = Camdenboss CTB0158-3 [part_number=CTB0158-3 package=THT]
  100 = Resistor [tolerance=±5% power=0.25W resistance=100 package=THT]
  IRLZ44N2 = Basic FET N-Channel [package="TO220 [THT]"]
  IR_LED_940_TSAL6200 = LED - 5mm [color="Infrared (940nm)" current=0.030A package="5 mm [THT]"]
  GDD = Camdenboss CTB0158-4 [part_number=CTB0158-4 package=THT]
  Pin_0_/_1 = Camdenboss CTB0158-3 [part_number=CTB0158-3 package=THT]
  5V = Camdenboss CTB0158-2 [part_number=CTB0158-2 package=THT]
  V3_3 = Camdenboss CTB0158-4 [part_number=CTB0158-4 package=THT]
  GY-NEO6MV3 = SUP500F [package=sup500f]
  TX_/_RX = Camdenboss CTB0158-2 [part_number=CTB0158-2 package=THT]
  DS18B20 = TEMPERATURE-SENSOR [package=to-92]
  DS18B20_2 = TEMPERATURE-SENSOR [package=to-92]
  100k = Resistor [tolerance=±5% power=0.25W resistance=100k package=THT]
  IR_LED_940_TSAL6201 = LED - 5mm [color="Infrared (940nm)" current=0.030A package="5 mm [THT]"]
  22 = Resistor [tolerance=±1% power=1W resistance=22 package=THT]
  22_2 = Resistor [tolerance=±5% power=0.25W resistance=22 package=THT]

nets:
  N1: ESP_outdoor.Pin_7, TX_/_RX.pin2
  N2: ESP_outdoor.Pin_8, TX_/_RX.pin1
  N3: ESP_outdoor.Pin_9, Pin_0_/_1.pin2, Pin_0_/_1.pin3
  N4: ESP_outdoor.Pin_10, Pin_0_/_1.pin1
  N5: ESP_outdoor.Pin_14, V3_3.pin1, V3_3.pin2, V3_3.pin3, V3_3.pin4
  N6: ESP_outdoor.Pin_15, GDD.pin1, GDD.pin2, GDD.pin3, GDD.pin4
  N7: ESP_outdoor.Pin_16, 5V.pin1, 5V.pin2
  N8: J1.pin1, 100.Pin_1
  N9: J1.pin2, 22.Pin_0, 22_2.Pin_1
  N10: J1.pin3, IRLZ44N2.source, 100k.Pin_0
  N11: J1.terminal_1, Pin_0_/_1.terminal_1
  N12: J1.terminal_2, 5V.terminal_2
  N13: J1.terminal_3, GDD.terminal_3
  N14: 100.Pin_0, IRLZ44N2.gate, 100k.Pin_1
  N15: IRLZ44N2.drain, IR_LED_940_TSAL6200.cathode, IR_LED_940_TSAL6201.cathode
  N16: IR_LED_940_TSAL6200.anode, 22_2.Pin_0
  N17: GDD.terminal_1, DS18B20.GND
  N18: GDD.terminal_2, DS18B20_2.GND
  N19: GDD.terminal_4, GY-NEO6MV3.GND
  N20: Pin_0_/_1.terminal_2, DS18B20_2.ADJ
  N21: Pin_0_/_1.terminal_3, DS18B20.ADJ
  N22: V3_3.terminal_2, GY-NEO6MV3.VCC
  N23: V3_3.terminal_3, DS18B20_2.VCC
  N24: V3_3.terminal_4, DS18B20.VCC
  N25: GY-NEO6MV3.RX-I, TX_/_RX.terminal_2
  N26: GY-NEO6MV3.TX-O, TX_/_RX.terminal_1
  N27: IR_LED_940_TSAL6201.anode, 22.Pin_1

custom parts:
  Esp32-c3 super mini: ESP32-C3 Development Board ESP32 SuperMini Development Board ESP32 Development Board WiFi Bluetooth.
